# Fritzing sketch wiring_blink_led (saved by Fritzing 0.9.3b)
breadboards: 1

parts:
  Part1 = Arduino Uno (Rev3)
  LED1 = LED - 5mm [color="Red (633nm)" package="5 mm [THT]"]
  R2 = Resistor [tolerance=±5% resistance=220 package=THT]

nets:
  N1: Part1.D3_PWM, LED1.anode
  N2: Part1.GND, R2.Pin_0
  N3: LED1.cathode, R2.Pin_1
