# Fritzing sketch wiring_button_led (saved by Fritzing 0.9.3b)
breadboards: 1

parts:
  Part1 = Arduino Uno (Rev3)
  LED1 = LED - 5mm [color="Red (633nm)" package="5 mm [THT]"]
  R2 = Resistor [tolerance=±5% resistance=220 package=THT]
  S1 = Pushbutton [package="[THT]"]
  R3 = Resistor [tolerance=±5% resistance=10k package=THT]

nets:
  N1: Part1.D3_PWM, LED1.anode
  N2: Part1.D5_PWM, S1.Pin_1, S1.Pin_2, R3.Pin_0
  N3: Part1.5V, R3.Pin_1
  N4: Part1.GND, R2.Pin_0, S1.Pin_3, S1.Pin_4
  N5: LED1.cathode, R2.Pin_1
