# Fritzing sketch wiring_photoresistor_led_dimmer (saved by Fritzing 0.9.3b)
breadboards: 1

parts:
  Part1 = Arduino Uno (Rev3)
  LED1 = LED - 5mm [color="Red (633nm)" package="5 mm [THT]"]
  R2 = Resistor [tolerance=±5% resistance=220 package=THT]
  R3 = Photocell (LDR) [package=THT]
  R4 = Resistor [tolerance=±5% resistance=10k package=THT]

nets:
  N1: Part1.A0, R3.pin_0, R4.Pin_1
  N2: Part1.D3_PWM, LED1.anode
  N3: Part1.5V, R2.Pin_0, R3.pin_1, R4.Pin_0
  N4: LED1.cathode, R2.Pin_1
