# Fritzing sketch wiring_potentiometer_led_dimmer (saved by Fritzing 0.9.3b)
breadboards: 1

parts:
  Part1 = Arduino Uno (Rev3)
  R1 = Rotary Potentiometer (Small) [maximum_resistance=10kΩ package=THT]
  LED1 = LED - 5mm [color="Red (633nm)" package="5 mm [THT]"]
  R2 = Resistor [tolerance=±5% resistance=220 package=THT]

nets:
  N1: Part1.A0, R1.wiper
  N2: Part1.D3_PWM, LED1.anode
  N3: Part1.5V, R1.leg1, R1.leg2, R2.Pin_0
  N4: LED1.cathode, R2.Pin_1
