# Fritzing sketch wiring_led_blink (saved by Fritzing 0.9.3b)
breadboards: 1

parts:
  Raspberry_Pi_B_rev1 = Raspberry Pi B rev1
  LED1 = LED - 5mm [color="Red (633nm)" package="5 mm [THT]"]
  R1 = Resistor [tolerance=±5% resistance=220 package=THT]

nets:
  N1: Raspberry_Pi_B_rev1.5V, Raspberry_Pi_B_rev1.GPIO_17, LED1.anode
  N2: Raspberry_Pi_B_rev1.GND, R1.Pin_0
  N3: LED1.cathode, R1.Pin_1
