# Fritzing sketch wiring_mcp3008_force_resistor (saved by Fritzing 0.9.3b)
breadboards: 1

parts:
  Raspberry_Pi_B_rev1 = Raspberry Pi B rev1
  IC1 = MCP3008 8-channel 10-bit ADC [part_number=MCP3008]
  R2 = Resistor [tolerance=±5% resistance=10k package=THT]
  J1 = Basic Force Sensing Resistor (FSR) [package=THT]

nets:
  N1: Raspberry_Pi_B_rev1.3V3, IC1.no_name_yet#15, IC1.no_name_yet#16, R2.Pin_0
  N2: Raspberry_Pi_B_rev1.GND, IC1.no_name_yet#9, IC1.no_name_yet#14, J1.pin_1
  N3: Raspberry_Pi_B_rev1.GPIO_10, IC1.no_name_yet#11
  N4: Raspberry_Pi_B_rev1.GPIO_9, IC1.no_name_yet#12
  N5: Raspberry_Pi_B_rev1.GPIO_11, IC1.no_name_yet#13
  N6: Raspberry_Pi_B_rev1.GPIO_8, IC1.no_name_yet#10
  N7: IC1.no_name_yet#1, R2.Pin_1, J1.pin_0

notes:
  Enable "SPI" in raspi-config under Interface
