# Fritzing sketch wiring_mcp3008_potentiometer (saved by Fritzing 0.9.3b)
breadboards: 1

parts:
  Raspberry_Pi_B_rev1 = Raspberry Pi B rev1
  IC1 = MCP3008 8-channel 10-bit ADC [part_number=MCP3008]
  R1 = Rotary Potentiometer (Small) [maximum_resistance=100kΩ package=THT]

nets:
  N1: Raspberry_Pi_B_rev1.3V3, IC1.no_name_yet#15, IC1.no_name_yet#16, R1.leg1
  N2: Raspberry_Pi_B_rev1.GND, IC1.no_name_yet#9, IC1.no_name_yet#14, R1.leg2
  N3: Raspberry_Pi_B_rev1.GPIO_10, IC1.no_name_yet#11
  N4: Raspberry_Pi_B_rev1.GPIO_9, IC1.no_name_yet#12
  N5: Raspberry_Pi_B_rev1.GPIO_11, IC1.no_name_yet#13
  N6: Raspberry_Pi_B_rev1.GPIO_8, IC1.no_name_yet#10
  N7: IC1.no_name_yet#1, R1.wiper

notes:
  Enable "SPI" in raspi-config under Interface
