# Fritzing sketch wiring_servo (saved by Fritzing 0.9.3b)

parts:
  J1 = Basic Servo
  Raspberry_Pi_B_rev1 = Raspberry Pi B rev1

nets:
  GND: J1.gnd, Raspberry_Pi_B_rev1.GND
  VCC: J1.vcc, Raspberry_Pi_B_rev1.5V
  N1: J1.pulse, Raspberry_Pi_B_rev1.GPIO_18

notes:
  BCM 18 (pin 12) is a special PWM pin
